# Fritzing sketch circuit (saved by Fritzing 0.8.7b)
breadboards: 1

parts:
  JACK = Audio Jack (TRRS) 3.5mm [part_number="LUMBERG JEITA RC-5325A" package="RC-5325A [SMD]"]
  C1 = Tantalum Capacitor [capacitance=1μF package="200 mil [THT, tantalum]"]
  JP1 = Header 3 [package=screwterminal-3.5mm-3_lock.007s]
  R1 = Resistor [tolerance=±10% resistance=47k package=THT]
  R2 = Resistor [tolerance=±10% resistance=10k package=THT]
  R3 = Resistor [tolerance=±10% resistance=10k package=THT]

nets:
  N1: JACK.TIP, C1.-
  N2: JACK.SLEEVE, R3.Pin_0
  N3: JACK.RING2, JP1.1, R1.Pin_0, R2.Pin_0
  N4: C1.+, JP1.2
  N5: JP1.3, R3.Pin_1

notes:
  Mic / Espruino TX / A9
  Headphone / Espruino RX / A10
  GND
