# Fritzing sketch circuit_single (saved by Fritzing 0.8.7b)
breadboards: 1

parts:
  C1 = Tantalum Capacitor [capacitance=1μF package="200 mil [THT, tantalum]"]
  R1 = Resistor [tolerance=±10% resistance=47k package=THT]
  U1 = 3.5mm Audio Jack [package=audio-jack]
  JP1 = Header 2 [package=screwterminal-3.5mm-2_lock]

nets:
  N1: C1.-, U1.RIGHT
  N2: C1.+, JP1.2
  N3: R1.Pin_0, U1.SLEEVE, JP1.1

notes:
  Headphone / Espruino RX / A10
  GND
